// Logisim project CPU.circ as structural Verilog: 3 circuits, main circuit main
module main (
);

  wire clock_1_out, decoder_1_out1, decoder_1_out2, decoder_1_out3, not_1_out, or_1_out, undriven,
       undriven_2, undriven_3, undriven_4;
  wire [1:0] counter_1_q, demultiplexer_1_out0, demultiplexer_1_out1, demultiplexer_1_out2,
       demultiplexer_1_out3, IR_q, IR_q_2, multiplexer_1_out, rom_1_data_3;
  wire [3:0] alu_1_flags_cgez, and_1_out, IR_q_3, register_1_q, rom_1_data;
  wire [4:0] counter_2_q;
  wire [7:0] controlled_buffer_1_out, R0_q, R1_q, R2_q, R3_q, register_2_q;
  wire [15:0] pc_1_out_4, pc_1_probe, rom_1_data_2;

  Clock clock_1 (.out(clock_1_out));
  Decoder #(.enable("false"), .select(2)) decoder_1 (
    .out1(decoder_1_out1), .out2(decoder_1_out2), .out3(decoder_1_out3), .sel(counter_1_q));  // open: out0
  Counter #(.max('h3), .width(2)) counter_1 (
    .Q(counter_1_q), .clk(clock_1_out));  // open: load, D, count, carry, up, clr
  assign controlled_buffer_1_out = demultiplexer_1_out0[0] ? R0_q : 8'bz;  // Controlled_Buffer controlled_buffer_1
  Register R0 (.D(controlled_buffer_1_out), .Q(R0_q), .clk(demultiplexer_1_out0[1]), .clr(undriven));  // open: en
  or or_1 (or_1_out, decoder_1_out1, decoder_1_out2, decoder_1_out3);
  assign controlled_buffer_1_out = demultiplexer_1_out1[0] ? R1_q : 8'bz;  // Controlled_Buffer controlled_buffer_2
  Register R1 (.D(controlled_buffer_1_out), .Q(R1_q), .clk(demultiplexer_1_out1[1]), .clr(undriven_2));  // open: en
  or or_2 (counter_2_q[4], and_1_out[0], and_1_out[1], and_1_out[2], and_1_out[3]);
  Counter #(.max('hf), .trigger("falling"), .width(4)) counter_2 (
    .Q(counter_2_q[3:0]), .clk(decoder_1_out3));  // open: load, D, count, carry, up, clr
  ROM #(.addrWidth(9), .dataWidth(16)) rom_1 (
    .addr({IR_q_3, counter_2_q}), .data({rom_1_data_2[15], rom_1_data_3, rom_1_data, rom_1_data_2[8:0]}));
  assign controlled_buffer_1_out = demultiplexer_1_out2[0] ? R2_q : 8'bz;  // Controlled_Buffer controlled_buffer_3
  Register R2 (.D(controlled_buffer_1_out), .Q(R2_q), .clk(demultiplexer_1_out2[1]), .clr(undriven_3));  // open: en
  assign and_1_out = {IR_q_2, IR_q} & register_1_q;  // AND_Gate and_1, 4 bits wide
  assign controlled_buffer_1_out = demultiplexer_1_out3[0] ? R3_q : 8'bz;  // Controlled_Buffer controlled_buffer_4
  Register R3 (.D(controlled_buffer_1_out), .Q(R3_q), .clk(demultiplexer_1_out3[1]), .clr(undriven_4));  // open: en
  Multiplexer #(.width(2)) multiplexer_1 (.in0(IR_q), .in1(IR_q_2), .out(multiplexer_1_out), .sel(rom_1_data_2[15]));
  // Probe on pc_1_probe
  PC pc_1 (.ctrl(rom_1_data), .in_1(controlled_buffer_1_out), .probe(pc_1_probe), .out_4(pc_1_out_4));
  Demultiplexer #(.select(2), .width(2)) demultiplexer_1 (
    .out0(demultiplexer_1_out0), .out1(demultiplexer_1_out1), .out2(demultiplexer_1_out2),
    .out3(demultiplexer_1_out3), .in(rom_1_data_3), .sel(multiplexer_1_out));
  // Probe on pc_1_out_4
  // Probe on controlled_buffer_1_out
  // Probe on controlled_buffer_1_out
  // Probe on controlled_buffer_1_out
  Register IR (.D(controlled_buffer_1_out), .Q({IR_q_3, IR_q_2, IR_q}), .clk(rom_1_data_2[8]));  // open: en, clr
  // Probe on {IR_q_3, IR_q_2, IR_q}
  // Probe on pc_1_out_4
  Register #(.width(4)) register_1 (.D(alu_1_flags_cgez), .Q(register_1_q), .clk(rom_1_data_2[1]));  // open: en, clr
  RAM #(.addrWidth(16), .databus("bidir")) ram_1 (
    .addr(pc_1_out_4), .we(not_1_out), .oe(rom_1_data_2[6]), .clk(rom_1_data_2[7]),
    .data(controlled_buffer_1_out));
  not not_1 (not_1_out, rom_1_data_2[6]);
  Register register_2 (.D(controlled_buffer_1_out), .Q(register_2_q), .clk(rom_1_data_2[5]));  // open: en, clr
  ALU alu_1 (
    .OP(rom_1_data_2[3:2]), .C_In(rom_1_data_2[4]), .B(register_2_q), .A(controlled_buffer_1_out),
    .in_4(rom_1_data_2[0]), .Flags_CGEZ(alu_1_flags_cgez), .O(controlled_buffer_1_out));

  // Notes on the sheet:
  //   contents of rom_1 (hex, n*v repeats v):
  //   16*0 ffff
endmodule

module ALU (
  input  C_In,
  input  [7:0] B,
  input  [7:0] A,
  input  in_4,
  input  [1:0] OP,
  output [7:0] O,
  output [3:0] Flags_CGEZ
);

  wire [7:0] adder_1_out, demultiplexer_1_out0, demultiplexer_1_out1, demultiplexer_1_out2,
       demultiplexer_1_out3, demultiplexer_2_out0, demultiplexer_2_out1, demultiplexer_2_out2,
       demultiplexer_2_out3, shifter_1_out, shifter_2_out;

  Demultiplexer #(.select(2), .width(8)) demultiplexer_1 (
    .out0(demultiplexer_1_out0), .out1(demultiplexer_1_out1), .out2(demultiplexer_1_out2),
    .out3(demultiplexer_1_out3), .in(B), .sel(OP));
  Demultiplexer #(.select(2), .width(8)) demultiplexer_2 (
    .out0(demultiplexer_2_out0), .out1(demultiplexer_2_out1), .out2(demultiplexer_2_out2),
    .out3(demultiplexer_2_out3), .in(A), .sel(OP));
  Adder adder_1 (
    .a(demultiplexer_2_out2), .b(demultiplexer_1_out2), .out(adder_1_out), .cin(C_In), .cout(Flags_CGEZ[0]));
  Shifter shifter_1 (.in(demultiplexer_2_out1), .\dist (demultiplexer_1_out1[2:0]), .out(shifter_1_out));
  Shifter #(.shift("lr")) shifter_2 (
    .in(demultiplexer_2_out3), .\dist (demultiplexer_1_out3[2:0]), .out(shifter_2_out));
  Comparator comparator_1 (
    .a(demultiplexer_2_out0), .b(demultiplexer_1_out0), .gt(Flags_CGEZ[1]), .eq(Flags_CGEZ[2]));  // open: lt
  nor nor_1 (Flags_CGEZ[3], demultiplexer_2_out0[0], demultiplexer_2_out0[1], demultiplexer_2_out0[2], demultiplexer_2_out0[3], demultiplexer_2_out0[4], demultiplexer_2_out0[5], demultiplexer_2_out0[6], demultiplexer_2_out0[7]);
  Multiplexer #(.enable("true"), .select(2), .width(8)) multiplexer_1 (
    .in0(adder_1_out), .in1(shifter_1_out), .in2(shifter_2_out), .out(O), .sel(OP), .en(in_4));  // open: in3

  // Notes on the sheet:
  //   OP: pull=down
  //   C_In: pull=down
  //   B: pull=down
  //   A: pull=down
endmodule

module PC (
  input  [7:0] in_1,
  input  [3:0] ctrl,
  output [15:0] probe,
  output [15:0] out_4
);

  wire and_1_out, and_2_out, and_3_out, and_4_out, and_5_out, counter_1_carry, not_1_out, not_2_out;

  not not_1 (not_1_out, ctrl[3]);
  not not_2 (not_2_out, ctrl[2]);
  and and_1 (and_1_out, not_1_out, not_2_out);
  and and_2 (and_2_out, ctrl[3], not_2_out);
  Counter counter_1 (
    .load(and_2_out), .D(in_1), .count(not_1_out), .Q(probe[7:0]), .carry(counter_1_carry), .up(and_1_out),
    .clk(ctrl[1]));  // open: clr
  and and_3 (and_3_out, not_1_out, not_2_out);
  and and_4 (and_4_out, ctrl[3], ctrl[2]);
  Counter counter_2 (
    .load(and_4_out), .D(in_1), .count(and_5_out), .Q(probe[15:8]), .up(and_3_out), .clk(ctrl[1]));  // open: carry, clr
  and and_5 (and_5_out, not_1_out, counter_1_carry);
  Pull_Resistor pull_resistor_1 (.node(out_4));
  assign out_4 = ctrl[0] ? probe : 16'bz;  // Controlled_Buffer controlled_buffer_1
endmodule
