// Logisim project CPU2.circ as structural Verilog
module mboard (
);

  wire and_1_out, and_2_out, and_3_out, and_4_out, clock_1_out, cpu_1_we, not_1_out;
  wire [7:0] cpu_1_dout, ram_1_data, rom_1_data;
  wire [15:0] cpu_1_addr;

  cpu cpu_1 (.CLK(clock_1_out), .DIN(cpu_1_dout), .WE(cpu_1_we), .DOUT(cpu_1_dout), .ADDR(cpu_1_addr));
  Clock clock_1 (.out(clock_1_out));
  // Probe on cpu_1_dout
  // Probe on cpu_1_addr
  and and_1 (and_1_out, ~cpu_1_addr[14], ~cpu_1_addr[15]);  // AND_Gate
  not not_1 (not_1_out, cpu_1_we);
  and and_2 (and_2_out, cpu_1_addr[14], cpu_1_addr[15]);
  and and_3 (and_3_out, not_1_out, and_1_out);
  and and_4 (and_4_out, and_1_out, ~not_1_out);  // AND_Gate
  Multiplexer #(.disabled("Z"), .width(8)) multiplexer_1 (
    .in1(ram_1_data), .out(cpu_1_dout), .sel(and_3_out));  // open: in0
  Multiplexer #(.disabled("Z"), .width(8)) multiplexer_2 (
    .in1(rom_1_data), .out(cpu_1_dout), .sel(and_2_out));  // open: in0
  RAM #(.addrWidth(14), .databus("bidir"), .enables("line")) ram_1 (
    .addr(cpu_1_addr[13:0]), .data(ram_1_data));  // open: we, oe, clk
  Multiplexer #(.disabled("Z"), .width(8)) multiplexer_3 (
    .in1(cpu_1_dout), .out(ram_1_data), .sel(and_4_out));  // open: in0
  ROM #(.addrWidth(14)) rom_1 (.addr(cpu_1_addr[13:0]), .data(rom_1_data));
endmodule

module cpu (
  input  [7:0] DIN,
  input  CLK,
  output [7:0] DOUT,
  output WE,
  output [15:0] ADDR
);

  wire A_D_sh, A_D_sl, ADR_out_5, ADR_out_6, C_D_sh, C_D_sl, counter_1_carry, counter_2_carry, PC_ct, PC_idh,
       PC_idl, PC_ldh, PC_ldl, SP_ct, SP_idh, SP_idl, SP_ldh, SP_ldl;
  wire [1:0] ctrl_1_m;
  wire [3:0] alu_1_z, ctrl_1_a_b, ctrl_1_c_d, ctrl_1_pc, ctrl_1_sp;
  wire [5:0] ctrl_1_alu;
  wire [7:0] A_D_tohigh, A_D_tolow, C_D_tohigh, C_D_tolow, counter_1_q, counter_2_q, counter_3_q,
       counter_4_q, ctrl_1_irprobe, multiplexer_2_out, register_1_q, register_2_q, register_3_q,
       register_4_q, register_5_q, register_6_q;

  // Probe on ctrl_1_irprobe
  // Probe on multiplexer_2_out
  Multiplexer #(.disabled("Z"), .width(8)) multiplexer_1 (.in1(multiplexer_2_out), .out(DOUT), .sel(WE));  // open: in0
  Multiplexer #(.disabled("Z"), .width(8)) multiplexer_2 (.in0(DIN), .out(multiplexer_2_out), .sel(WE));  // open: in1
  // Probe on ctrl_1_sp
  // Probe on ctrl_1_pc
  // Probe on ctrl_1_m
  // Probe on ctrl_1_c_d
  // Probe on ctrl_1_a_b
  ctrl ctrl_1 (
    .Clk(CLK), .DATABUS(multiplexer_2_out), .FLAG(alu_1_z), .A_B(ctrl_1_a_b), .ALU(ctrl_1_alu),
    .IRPROBE(ctrl_1_irprobe), .WE(WE), .PC(ctrl_1_pc), .SP(ctrl_1_sp), .M(ctrl_1_m), .C_D(ctrl_1_c_d));
  Counter counter_1 (
    .load(PC_ldl), .D(multiplexer_2_out), .count(PC_ct), .Q(counter_1_q), .carry(counter_1_carry),
    .up(PC_idl), .clk(CLK));  // open: clr
  Counter counter_2 (
    .load(SP_ldl), .D(multiplexer_2_out), .count(SP_ct), .Q(counter_2_q), .carry(counter_2_carry),
    .up(SP_idl), .clk(CLK));  // open: clr
  Register register_1 (.D(multiplexer_2_out), .en(ADR_out_6), .Q(register_1_q), .clk(CLK));  // open: clr
  Register register_2 (.D(C_D_tolow), .en(C_D_sl), .Q(register_2_q), .clk(CLK));  // open: clr
  Register register_3 (.D(A_D_tolow), .en(A_D_sl), .Q(register_3_q), .clk(CLK));  // open: clr
  // Probe on ADDR
  CNTR_CTRL PC (
    .olow(counter_1_q), .ohi(counter_3_q), .in_3(ctrl_1_sp), .out16(ADDR), .out8(multiplexer_2_out),
    .idh(PC_idh), .idl(PC_idl), .ldh(PC_ldh), .ldl(PC_ldl), .ct(PC_ct));
  Counter counter_3 (
    .load(PC_ldh), .D(counter_1_q), .count(counter_1_carry), .Q(counter_3_q), .up(PC_idh), .clk(CLK));  // open: carry, clr
  CNTR_CTRL SP (
    .olow(counter_2_q), .ohi(counter_4_q), .in_3(ctrl_1_pc), .out16(ADDR), .out8(multiplexer_2_out),
    .idh(SP_idh), .idl(SP_idl), .ldh(SP_ldh), .ldl(SP_ldl), .ct(SP_ct));
  Counter counter_4 (
    .load(SP_ldh), .D(counter_2_q), .count(counter_2_carry), .Q(counter_4_q), .up(SP_idh), .clk(CLK));  // open: carry, clr
  ADR_CTRL ADR (
    .in_3(ctrl_1_m), .SHFL(register_1_q), .SHFH(register_4_q), .out_5(ADR_out_5), .out_6(ADR_out_6),
    .out_4(ADDR));
  Register register_4 (.D(register_1_q), .en(ADR_out_5), .Q(register_4_q), .clk(CLK));  // open: clr
  REG_CRTL C_D (
    .In8(multiplexer_2_out), .in_2(ctrl_1_c_d), .FromLow(register_2_q), .FromHigh(register_5_q), .SH(C_D_sh),
    .Out8(multiplexer_2_out), .SL(C_D_sl), .ToLow(C_D_tolow), .ToHigh(C_D_tohigh));
  Register register_5 (.D(C_D_tohigh), .en(C_D_sh), .Q(register_5_q), .clk(CLK));  // open: clr
  REG_CRTL A_D (
    .In8(multiplexer_2_out), .in_2(ctrl_1_a_b), .FromLow(register_3_q), .FromHigh(register_6_q), .SH(A_D_sh),
    .Out8(multiplexer_2_out), .SL(A_D_sl), .ToLow(A_D_tolow), .ToHigh(A_D_tohigh));
  Register register_6 (.D(A_D_tohigh), .en(A_D_sh), .Q(register_6_q), .clk(CLK));  // open: clr
  ALU alu_1 (
    .A(register_3_q), .B(register_6_q), .cin(ctrl_1_alu[5]), .op3(ctrl_1_alu[4]), .op2(ctrl_1_alu[3]),
    .op1(ctrl_1_alu[2]), .op0(ctrl_1_alu[1]), .X(ctrl_1_alu[0]), .O(multiplexer_2_out), .Z(alu_1_z[0]),
    .G(alu_1_z[1]), .E(alu_1_z[2]), .C(alu_1_z[3]));
endmodule

module ALU (
  input  [7:0] A,
  input  [7:0] B,
  input  cin,
  input  op3,
  input  op2,
  input  op1,
  input  op0,
  input  X,
  output [7:0] O,
  output Z,
  output G,
  output E,
  output C
);

  wire adder_1_cout, subtractor_1_bout;
  wire [7:0] adder_1_out, and_1_out, demultiplexer_1_out0, demultiplexer_1_out1, demultiplexer_1_out2,
       demultiplexer_1_out3, demultiplexer_1_out4, demultiplexer_1_out5, demultiplexer_1_out6,
       demultiplexer_1_out7, demultiplexer_2_out0, demultiplexer_2_out1, demultiplexer_2_out2,
       demultiplexer_2_out3, demultiplexer_2_out4, demultiplexer_2_out6, demultiplexer_2_out7, not_1_out,
       or_1_out, shifter_1_out, shifter_2_out, subtractor_1_out, xor_1_out;

  Demultiplexer #(.select(3), .width(8)) demultiplexer_1 (
    .out0(demultiplexer_1_out0), .out1(demultiplexer_1_out1), .out2(demultiplexer_1_out2),
    .out3(demultiplexer_1_out3), .out4(demultiplexer_1_out4), .out5(demultiplexer_1_out5),
    .out6(demultiplexer_1_out6), .out7(demultiplexer_1_out7), .in(A), .sel({op2, op1, op0}));
  Demultiplexer #(.select(3), .width(8)) demultiplexer_2 (
    .out0(demultiplexer_2_out0), .out1(demultiplexer_2_out1), .out2(demultiplexer_2_out2),
    .out3(demultiplexer_2_out3), .out4(demultiplexer_2_out4), .out6(demultiplexer_2_out6),
    .out7(demultiplexer_2_out7), .in(B), .sel({op2, op1, op0}));  // open: out5
  Adder adder_1 (.a(demultiplexer_1_out0), .b(demultiplexer_2_out0), .out(adder_1_out), .cin(cin), .cout(adder_1_cout));
  Subtractor subtractor_1 (
    .a(demultiplexer_1_out1), .b(demultiplexer_2_out1), .out(subtractor_1_out), .bin(cin),
    .bout(subtractor_1_bout));
  assign and_1_out = demultiplexer_1_out2 & demultiplexer_2_out2;  // AND_Gate and_1, 8 bits wide
  assign or_1_out = demultiplexer_1_out3 | demultiplexer_2_out3;  // OR_Gate or_1, 8 bits wide
  assign xor_1_out = demultiplexer_1_out4 ^ demultiplexer_2_out4;  // XOR_Gate xor_1, 8 bits wide
  assign not_1_out = ~demultiplexer_1_out5;  // NOT_Gate not_1, 8 bits wide
  Shifter #(.shift("rl")) shifter_1 (
    .in(demultiplexer_1_out6), .\dist (demultiplexer_2_out6[2:0]), .out(shifter_1_out));
  Shifter #(.shift("rr")) shifter_2 (
    .in(demultiplexer_1_out7), .\dist (demultiplexer_2_out7[2:0]), .out(shifter_2_out));
  Multiplexer #(.disabled("Z"), .enable("true"), .select(3), .width(8)) multiplexer_1 (
    .in0(adder_1_out), .in1(subtractor_1_out), .in2(and_1_out), .in3(or_1_out), .in4(xor_1_out),
    .in5(not_1_out), .in6(shifter_1_out), .in7(shifter_2_out), .out(O), .sel({op2, op1, op0}), .en(X));
  nor nor_1 (Z, A[0], A[1], A[2], A[3], A[4], A[5], A[6], A[7]);
  Comparator comparator_1 (.a(A), .b(B), .gt(G), .eq(E));  // open: lt
  or or_2 (C, adder_1_cout, subtractor_1_bout);

  // Notes on the sheet:
  //   A: pull=down
  //   B: pull=down
endmodule

module ctrl (
  input  Clk,
  input  [7:0] DATABUS,
  input  [3:0] FLAG,
  output [7:0] IRPROBE,
  output WE,
  output [3:0] PC,
  output [3:0] SP,
  output [1:0] M,
  output [3:0] C_D,
  output [3:0] A_B,
  output [5:0] ALU
);

  wire not_1_out, pull_resistor_1_node;
  wire [2:0] counter_1_q, rom_1_data;
  wire [3:0] and_1_out, decoder_1_out3, register_2_q;
  wire [11:11] or_1_out;
  wire [31:28] rom_1_data_2;

  Register register_1 (.D(DATABUS), .en(rom_1_data[1]), .Q(IRPROBE), .clk(Clk));  // open: clr
  Pull_Resistor #(.pull(1)) pull_resistor_1 (.node(pull_resistor_1_node));
  Decoder #(.enable("false"), .select(2)) decoder_1 (
    .out0(decoder_1_out3[3]), .out1(decoder_1_out3[2]), .out2(decoder_1_out3[1]), .out3(decoder_1_out3[0]),
    .sel(IRPROBE[1:0]));
  Register #(.width(4)) register_2 (.D(FLAG), .Q(register_2_q), .clk(Clk));  // open: en, clr
  not not_1 (not_1_out, pull_resistor_1_node);
  Counter #(.max('h7), .trigger("falling"), .width(3)) counter_1 (
    .load(not_1_out), .count(pull_resistor_1_node), .Q(counter_1_q), .up(pull_resistor_1_node), .clk(Clk),
    .clr(rom_1_data[0]));  // open: D, carry
  assign and_1_out = decoder_1_out3 & register_2_q;  // AND_Gate and_1, 4 bits wide
  or or_1 (or_1_out[11], and_1_out[0], and_1_out[1], and_1_out[2], and_1_out[3]);
  ROM #(.addrWidth(12), .dataWidth(32)) rom_1 (
    .addr({or_1_out[11], IRPROBE, counter_1_q}),
    .data({rom_1_data_2, rom_1_data, WE, PC, SP, M, C_D, A_B, ALU}));
  Pull_Resistor pull_resistor_2 (.node({rom_1_data_2, rom_1_data, WE, PC, SP, M, C_D, A_B, ALU}));

  // Notes on the sheet:
  //   Clk: pull=down
  //   contents of rom_1 (hex, n*v repeats v):
  //   10000280 8000000 6*0 10000280 7*0 10000280 7*0 10000280 7*0 10000280 7*0 10000280 7*0 10000280 7*0
  //   10000280 7*0 10000280 8000000 6*0 10000280 7*0 10000280 7*0 10000280 7*0 10000280 7*0 10000280 7*0
  //   10000280 7*0 10000280 7*0 10000280 400280 8000000 5*0 10000280 7*0 10000280 7*0 10000280 7*0
  //   10000280 7*0 10000280 7*0 10000280 7*0 10000280 7*0 10000280 7*0 10000280 7*0 10000280 7*0 10000280
  //   7*0 10000280 7*0 10000280 7*0 10000280 7*0 10000280 7*0 10000280 7*0 10000280 7*0 10000280 7*0
  //   10000280 7*0 10000280 7*0 10000280 7*0 10000280 7*0 10000280 7*0 10000280 7*0 10000280 7*0 10000280
  //   7*0 10000280 7*0 10000280 7*0 10000280 7*0 10000280 7*0 10000280 7*0 10000280 7*0 10000280 7*0
  //   10000280 7*0 10000280 7*0 10000280 7*0 10000280 7*0 10000280 7*0 10000280 7*0 10000280 7*0 10000280
  //   7*0 10000280 7*0 10000280 7*0 10000280 7*0 10000280 7*0 10000280 7*0 10000280 7*0 10000280 7*0
  //   10000280 7*0 10000280 7*0 10000280 7*0 10000280 7*0 10000280 7*0 10000280 7*0 10000280 7*0 10000280
  //   7*0 10000280 7*0 10000280 7*0 10000280 7*0 10000280 7*0 10000280 7*0 10000280 7*0 10000280 7*0
  //   10000280 7*0 10000280 7*0 10000280 7*0 10000280 7*0 10000280 7*0 10000280 7*0 10000280 7*0 10000280
  //   7*0 10000280 7*0 10000280 7*0 10000280 7*0 10000280 7*0 10000280 7*0 10000280 7*0 10000280 7*0
  //   10000280 7*0 10000280 7*0 10000280 7*0 10000280 7*0 10000280 7*0 10000280 7*0 10000280 7*0 10000280
  //   7*0 10000280 7*0 10000280 7*0 10000280 7*0 10000280 7*0 10000280 7*0 10000280 7*0 10000280 7*0
  //   10000280 7*0 10000280 7*0 10000280 7*0 10000280 7*0 10000280 7*0 10000280 7*0 10000280 7*0 10000280
  //   7*0 10000280 7*0 10000280 7*0 10000280 7*0 10000280 7*0 10000280 7*0 10000280 7*0 10000280 7*0
  //   10000280 7*0 10000280 7*0 10000280 7*0 10000280 7*0 10000280 7*0 10000280 7*0 10000280 7*0 10000280
  //   7*0 10000280 7*0 10000280 7*0 10000280 7*0 10000280 7*0 10000280 7*0 10000280 7*0 10000280 7*0
  //   10000280 7*0 10000280 7*0 10000280 7*0 10000280 7*0 10000280 7*0 10000280 7*0 10000280 7*0 10000280
  //   7*0 10000280 7*0 10000280 7*0 10000280 7*0 10000280 7*0 10000280 7*0 10000280 7*0 10000280 7*0
  //   10000280 7*0 10000280 7*0 10000280 7*0 10000280 7*0 10000280 7*0 10000280 7*0 10000280 7*0 10000280
  //   7*0 10000280 7*0 10000280 7*0 10000280 7*0 10000280 7*0 10000280 7*0 10000280 7*0 10000280 7*0
  //   10000280 7*0 10000280 7*0 10000280 7*0 10000280 7*0 10000280 7*0 10000280 7*0 10000280 7*0 10000280
  //   7*0 10000280 7*0 10000280 7*0 10000280 7*0 10000280 7*0 10000280 7*0 10000280 7*0 10000280 7*0
  //   10000280 7*0 10000280 7*0 10000280 7*0 10000280 7*0 10000280 7*0 10000280 7*0 10000280 7*0 10000280
  //   7*0 10000280 7*0 10000280 7*0 10000280 7*0 10000280 7*0 10000280 7*0 10000280 7*0 10000280 7*0
  //   10000280 7*0 10000280 7*0 10000280 7*0 10000280 7*0 10000280 7*0 10000280 7*0 10000280 7*0 10000280
  //   7*0 10000280 7*0 10000280 7*0 10000280 7*0 10000280 7*0 10000280 7*0 10000280 7*0 10000280 7*0
  //   10000280 7*0 10000280 7*0 10000280 7*0 10000280 7*0 10000280 7*0 10000280 7*0 10000280 7*0 10000280
  //   7*0 10000280 7*0 10000280 7*0 10000280 7*0 10000280 7*0 10000280 7*0 10000280 7*0 10000280 7*0
  //   10000280 7*0 10000280 7*0 10000280 7*0 10000280 7*0 10000280 7*0 10000280 7*0 10000280 7*0 10000280
  //   7*0 10000280 7*0 10000280 7*0 10000280 7*0 10000280 7*0 10000280 7*0 10000280 7*0 10000280 7*0
  //   10000280 7*0 10000280 7*0 10000280 7*0 10000280 7*0 10000280 7*0 10000280 7*0 10000280 7*0 10000280
  //   7*0 10000280 7*0 10000280 7*0 10000280
endmodule

module REG_CRTL (
  input  [7:0] In8,
  input  [3:0] in_2,
  input  [7:0] FromLow,
  input  [7:0] FromHigh,
  output [7:0] Out8,
  output SH,
  output SL,
  output [7:0] ToLow,
  output [7:0] ToHigh
);

  Multiplexer #(.disabled("Z"), .enable("true"), .width(8)) multiplexer_1 (
    .in0(FromLow), .in1(FromHigh), .out(Out8), .sel(in_2[0]), .en(in_2[1]));

  assign SH = in_2[3];
  assign SL = in_2[2];
  assign ToHigh = In8;
  assign ToLow = In8;
endmodule

module CNTR_CTRL (
  input  [7:0] olow,
  input  [7:0] ohi,
  input  [3:0] in_3,
  output [15:0] out16,
  output [7:0] out8,
  output idh,
  output idl,
  output ldh,
  output ldl,
  output ct
);

  assign out16 = in_3[3] ? {ohi, olow} : 16'bz;  // Controlled_Buffer controlled_buffer_1
  assign out8 = in_3[2] ? ohi : 8'bz;  // Controlled_Buffer controlled_buffer_2
  and and_1 (idh, in_3[1], ~in_3[0]);  // AND_Gate
  and and_2 (ldh, ~in_3[1], in_3[0]);  // AND_Gate

  assign ct = in_3[1];
  assign idl = idh;
  assign ldl = ldh;
endmodule

module ADR_CTRL (
  input  [7:0] SHFL,
  input  [7:0] SHFH,
  input  [1:0] in_3,
  output [15:0] out_4,
  output out_5,
  output out_6
);

  assign out_4 = in_3[1] ? {SHFH, SHFL} : 16'bz;  // Controlled_Buffer controlled_buffer_1

  assign out_5 = in_3[0];
  assign out_6 = in_3[0];
endmodule
